// Logisim project IA39mips.circ as structural Verilog: 1 circuit, main circuit MIPS
module MIPS (
);

  wire clk, clock_1_out, FPC, halt, lw;
  wire [3:0] control_alu_1_out;
  wire [5:0] CODEOP;
  wire [27:0] PC_4;
  wire [31:0] IB, multiplexer_1_out, pc_1_pc;
  wire [31:2] DE_J;

  Clock #(.highDuration(10), .lowDuration(10)) clock_1 (.out(clock_1_out));
  Multiplexer #(.width(32), .enable("false")) multiplexer_1 (
    .in0({DE_J[31:28], PC_4}), .in1({DE_J, 2'b00}), .out(multiplexer_1_out), .sel(FPC));
  PC pc_1 (.IN(multiplexer_1_out), .PC(pc_1_pc), .clk(clk));
  // Probe on pc_1_pc
  and and_1 (halt, CODEOP[5], CODEOP[4], CODEOP[3], CODEOP[2], CODEOP[1], CODEOP[0]);
  ClockGen clockgen_1 (.halt(halt), .clkin(clock_1_out), .clkout(clk));
  Adder #(.width(32)) adder_1 (.a(32'h4), .b(pc_1_pc), .out({DE_J[31:28], PC_4}), .cin(1'b0));  // open: cout
  InstDecoder instdecoder_1 (
    .IB(IB), .IB31_26(CODEOP), .IB25_0(DE_J[27:2]));  // open: IB25_21, IB20_16, IB15_11, IB5_0, IB15_0
  and and_2 (FPC, ~CODEOP[5], ~CODEOP[4], ~CODEOP[3], ~CODEOP[2], CODEOP[1], ~CODEOP[0]);  // AND_Gate
  Instruction_memory instruction_memory_1 (.Read_address(pc_1_pc), .Instruction(IB));
  and and_3 (lw, CODEOP[5], ~CODEOP[4], ~CODEOP[3], ~CODEOP[2], CODEOP[1], CODEOP[0]);  // AND_Gate
  // Probe on IB
  Register_file register_file_1 (.clk(clk));  // open: Read_Register_1, Read_Register_2, Write_Register, Write_Data, Read_Data_1, Read_Data_2, Write
  Control_ALU control_alu_1 (.OUT(control_alu_1_out));  // open: OpALU, funcion
  ALU alu_1 (.Operation(control_alu_1_out));  // open: A, B, Z, Result
  Data_Memory_32 data_memory_32_1 (.clk(clk));  // open: Address, Write_Data, Read_Data, Write, Read

  // Other names for the same wires on the sheet: DIR[25:0] = DE_J[27:2]; PC_4[31:28] = DE_J[31:28]; j = FPC
endmodule
